// Logisim project CS1501_U201514477_华龙_cpu.circ as structural Verilog: 3 circuits, main circuit MIPS CPU
module MIPS_CPU (
);

  wire ALU_Equal, ALU_R_0, and_3_out, and_4_out, and_5_out, beq, bltz, bne, branch, clk, clock_1_out,
       comparator_1_eq, controlled_buffer_1_out, d_ff_1_q, d_ff_2_q, d_ff_2_qn, d_ff_3_q, display__a0, halt,
       not_1_out, not_2_out, not_3_out, not_4_out, pull_resistor_1_node, \单步执行_out , \清零_2_out , \清零_out ,
       \运行_暂停_out ;
  wire [3:0] ALUOP;
  wire [4:0] multiplexer_4_out, multiplexer_5_out, multiplexer_6_out, multiplexer_7_out;
  wire [15:0] multiplexer_17_out;
  wire [16:0] multiplexer_8_out, multiplexer_9_out, multiplexer_10_out;
  wire [23:0] control_signal, mips_ram_1_p1;
  wire [27:2] rom_1_data;
  wire [31:0] adder_1_out, bit_extender_1_out, mips_ram_1_p5, multiplexer_1_out, multiplexer_2_out,
       multiplexer_3_out, multiplexer_11_out, multiplexer_12_out, multiplexer_13_out, multiplexer_14_out,
       PC_1, PC_q, pull_resistor_2_node, pull_resistor_3_node, RF_A, RF_B, \数码管锁存_q ;
  wire [31:1] alu_1_result;
  wire [31:26] rom_1_data_2;

  Multiplexer #(.width(32), .enable("false")) multiplexer_1 (
    .in0(multiplexer_2_out), .in1(multiplexer_3_out), .out(multiplexer_1_out), .sel(control_signal[9]));
  // Probe on multiplexer_1_out
  not not_1 (not_1_out, halt);
  Button \u_运行_暂停  (.out(\运行_暂停_out ));
  D_Flip_Flop #(.trigger("falling")) d_ff_1 (.clk(clk), .D(halt), .Q(d_ff_1_q));  // open: Qn, preset, en, reset
  Multiplexer #(.width(32), .enable("false")) multiplexer_2 (
    .in0(PC_1), .in1(adder_1_out), .out(multiplexer_2_out), .sel(branch));
  Multiplexer #(.width(32), .enable("false")) multiplexer_3 (
    .in0({PC_1[31:28], rom_1_data, 2'b00}), .in1(RF_A), .out(multiplexer_3_out), .sel(control_signal[8]));
  PC_1 pc_1_1 (.PC(PC_q), .PC_4(PC_1));
  Register #(.width(32)) PC (.D(multiplexer_1_out), .en(not_1_out), .Q(PC_q), .clk(clk), .clr(\清零_out ));
  Button \u_清零  (.out(\清零_out ));
  Clock clock_1 (.out(clock_1_out));
  assign controlled_buffer_1_out = d_ff_2_q ? clock_1_out : 1'bz;  // Controlled_Buffer controlled_buffer_1
  D_Flip_Flop d_ff_2 (.clk(\运行_暂停_out ), .D(d_ff_2_qn), .Q(d_ff_2_q), .Qn(d_ff_2_qn));  // open: preset, en, reset
  Pull_Resistor pull_resistor_1 (.node(pull_resistor_1_node));
  Button \u_单步执行  (.out(\单步执行_out ));
  Register #(.width(32)) \u_数码管锁存  (.D(RF_B), .en(display__a0), .Q(\数码管锁存_q ), .clk(clk));  // open: clr
  D_Flip_Flop #(.trigger("falling")) d_ff_3 (.clk(clk), .D(d_ff_1_q), .Q(d_ff_3_q));  // open: Qn, preset, en, reset
  not not_2 (not_2_out, d_ff_3_q);
  Comparator #(.width(32), .mode("unsigned")) comparator_1 (
    .a(PC_q), .b({32{1'b1}}), .eq(comparator_1_eq));  // open: gt, lt
  not not_3 (not_3_out, comparator_1_eq);
  assign pull_resistor_1_node = not_3_out ? controlled_buffer_1_out : 1'bz;  // Controlled_Buffer controlled_buffer_2
  xor xor_1 (clk, pull_resistor_1_node, \单步执行_out );
  Hex_Digit_Display hex_digit_display_1 (.value(\数码管锁存_q [31:28]));  // open: dp
  Hex_Digit_Display hex_digit_display_2 (.value(\数码管锁存_q [27:24]));  // open: dp
  Counter #(.width(32), .max('hffffffff), .trigger("falling")) counter_1 (
    .count(not_2_out), .clk(clk), .clr(\清零_2_out ));  // open: load, D, Q, carry
  Button \u_清零_2  (.out(\清零_2_out ));
  ROM #(.addrWidth(10), .dataWidth(32)) rom_1 (.addr(PC_q[11:2]), .data({rom_1_data_2, rom_1_data}));  // open: sel
  Hex_Digit_Display hex_digit_display_3 (.value(\数码管锁存_q [23:20]));  // open: dp
  Hex_Digit_Display hex_digit_display_4 (.value(\数码管锁存_q [19:16]));  // open: dp
  Hex_Digit_Display hex_digit_display_5 (.value(\数码管锁存_q [11:8]));  // open: dp
  Hex_Digit_Display hex_digit_display_6 (.value(\数码管锁存_q [15:12]));  // open: dp
  MIPS_Controller mips_controller_1 (
    .OP(rom_1_data_2), .Funct(rom_1_data[7:2]),
    .\控制信号 ({ALUOP, control_signal[23:8], beq, bne, bltz, control_signal[4:0]}));
  Multiplexer #(.width(5), .enable("false")) multiplexer_4 (
    .in0(rom_1_data[22:18]), .in1(rom_1_data[17:13]), .out(multiplexer_4_out), .sel(control_signal[21]));
  Hex_Digit_Display hex_digit_display_7 (.value(\数码管锁存_q [7:4]));  // open: dp
  Hex_Digit_Display hex_digit_display_8 (.value(\数码管锁存_q [3:0]));  // open: dp
  Multiplexer #(.width(5), .enable("false")) multiplexer_5 (
    .in0(rom_1_data[27:23]), .in1(5'b00010), .out(multiplexer_5_out), .sel(control_signal[23]));
  Multiplexer #(.width(5), .enable("false")) multiplexer_6 (
    .in0(rom_1_data[22:18]), .in1(5'b00100), .out(multiplexer_6_out), .sel(control_signal[22]));
  Multiplexer #(.width(5), .enable("false")) multiplexer_7 (
    .in0(multiplexer_4_out), .in1({5{1'b1}}), .out(multiplexer_7_out), .sel(control_signal[20]));
  Multiplexer #(.width(17), .enable("false")) multiplexer_8 (
    .in0(17'ha), .in1({{12{1'b0}}, rom_1_data[12:8]}), .out(multiplexer_8_out), .sel(control_signal[12]));
  Multiplexer #(.width(17), .enable("false")) multiplexer_9 (
    .in0(multiplexer_8_out), .in1(multiplexer_10_out), .out(multiplexer_9_out), .sel(control_signal[11]));
  Multiplexer #(.width(17), .enable("false")) multiplexer_10 (
    .in0({{2{rom_1_data[17]}}, rom_1_data[16:2]}), .in1({1'b0, rom_1_data[17:2]}), .out(multiplexer_10_out),
    .sel(control_signal[10]));
  Multiplexer #(.width(32), .enable("false")) multiplexer_11 (
    .in0({alu_1_result[31:26], mips_ram_1_p1, alu_1_result[1], ALU_R_0}), .in1(PC_1),
    .out(multiplexer_11_out), .sel(control_signal[18]));
  Multiplexer #(.width(32), .enable("false")) multiplexer_12 (
    .in0(multiplexer_11_out), .in1(multiplexer_13_out), .out(multiplexer_12_out), .sel(control_signal[17]));
  Multiplexer #(.width(32), .enable("false")) multiplexer_13 (
    .in0(mips_ram_1_p5), .in1({{16{1'b0}}, multiplexer_17_out}), .out(multiplexer_13_out),
    .sel(control_signal[16]));
  // Probe on multiplexer_7_out
  assign bit_extender_1_out = {{15{multiplexer_9_out[16]}}, multiplexer_9_out};  // Bit_Extender bit_extender_1
  // RegisterFile registerfile_1: pin names not known; wires that end beside it: multiplexer_12_out, clk, control_signal[19], multiplexer_7_out, multiplexer_5_out, multiplexer_6_out, RF_A, RF_B
  // Probe on multiplexer_6_out
  // Probe on multiplexer_5_out
  Multiplexer #(.width(32), .enable("false")) multiplexer_14 (
    .in0(RF_B), .in1(RF_A), .out(multiplexer_14_out), .sel(control_signal[14]));
  Adder #(.width(32)) adder_1 (.a(PC_1), .b({bit_extender_1_out[29:0], 2'b00}), .out(adder_1_out));  // open: cin, cout
  Pull_Resistor pull_resistor_2 (.node(pull_resistor_2_node));
  Multiplexer #(.width(32), .enable("false")) multiplexer_15 (
    .in0(RF_A), .in1(RF_B), .out(pull_resistor_2_node), .sel(control_signal[15]));
  Pull_Resistor pull_resistor_3 (.node(pull_resistor_3_node));
  Multiplexer #(.width(32), .enable("false")) multiplexer_16 (
    .in0(multiplexer_14_out), .in1(bit_extender_1_out), .out(pull_resistor_3_node), .sel(control_signal[13]));
  Pull_Resistor #(.pull(1)) pull_resistor_4 (.node(ALUOP));
  // MIPS_RAM mips_ram_1: pin names not known; wires that end beside it: mips_ram_1_p1, RF_B, control_signal[3], clk, mips_ram_1_p5
  // Probe on mips_ram_1_p5
  ALU alu_1 (
    .AluOP(ALUOP), .X(pull_resistor_2_node), .Equal(ALU_Equal),
    .Result({alu_1_result[31:26], mips_ram_1_p1, alu_1_result[1], ALU_R_0}), .Y(pull_resistor_3_node));  // open: Signed_Overflow, Result_2, UnSigned_Overflow
  Multiplexer #(.width(16), .enable("false")) multiplexer_17 (
    .in0(mips_ram_1_p5[15:0]), .in1(mips_ram_1_p5[31:16]), .out(multiplexer_17_out), .sel(alu_1_result[1]));
  and and_1 (halt, control_signal[4], ~not_4_out);  // AND_Gate
  and and_2 (display__a0, control_signal[4], not_4_out);
  not not_4 (not_4_out, ALU_Equal);
  and and_3 (and_3_out, ALU_Equal, beq);
  and and_4 (and_4_out, ~ALU_Equal, bne);  // AND_Gate
  and and_5 (and_5_out, ALU_R_0, bltz);
  or or_1 (branch, and_3_out, and_4_out, and_5_out);

  // Other names for the same wires on the sheet: DM_WE = control_signal[3]; syscall = control_signal[4];
  //   control_signal (some bits) = {ALUOP, beq, bne, bltz}; jump_register = control_signal[8];
  //   jump = control_signal[9]; zero_ext_IMM = control_signal[10]; extend_IMM = control_signal[11];
  //   extend_shamt = control_signal[12]; Y__S_EXT = control_signal[13]; Y__RF_A = control_signal[14];
  //   X__RF_B = control_signal[15]; Din__DM_half = control_signal[16]; Din__DM = control_signal[17];
  //   Din__PC_1 = control_signal[18]; RF_WE = control_signal[19]; rW__GPR_31 = control_signal[20];
  //   rW__rd = control_signal[21]; rB___a0 = control_signal[22]; rA___v0 = control_signal[23]

  // Notes on the sheet:
  //   contents of rom_1 (hex, n*v repeats v):
  //   20110001 8000c05 20110001 20120002 20130003 8000c09 20110001 20120002 20130003 8000c0d 20110001
  //   20120002 20130003 8000c11 20110001 20120002 20130003 c000cb8 20100001 20110001 118fc0 112020
  //   20020022 c 118882 12200001 8000c15 112020 20020022 c 20110001 118880 112020 20020022 c 12200001
  //   8000c1f 20110001 118fc0 112020 20020022 c 1188c3 112020 20020022 c 118903 112020 20020022 c 118903
  //   112020 20020022 c 118903 112020 20020022 c 118903 112020 20020022 c 118903 112020 20020022 c 118903
  //   112020 20020022 c 118903 112020 20020022 c 20100001 109fc0 139fc3 8021 2012000c 24160003 26100001
  //   3210000f 20080008 20090001 139900 2709825 132020 20020022 c 1094022 1500fff9 22100001 2018000f
  //   2188024 108700 20080008 20090001 139902 2709825 132021 20020022 c 1094022 1500fff9 108702 2c9b022
  //   12c00001 8000c50 4020 1084027 84400 3508ffff 82021 20020022 c 2010ffff 20110000 ae300000 22100001
  //   22310004 ae300000 22100001 22310004 ae300000 22100001 22310004 ae300000 22100001 22310004 ae300000
  //   22100001 22310004 ae300000 22100001 22310004 ae300000 22100001 22310004 ae300000 22100001 22310004
  //   ae300000 22100001 22310004 ae300000 22100001 22310004 ae300000 22100001 22310004 ae300000 22100001
  //   22310004 ae300000 22100001 22310004 ae300000 22100001 22310004 ae300000 22100001 22310004 ae300000
  //   22100001 22310004 22100001 8020 2011003c 8e130000 8e340000 274402a 11000002 ae330000 ae140000
  //   2231fffc 1611fff8 102020 20020022 c 22100004 2011003c 1611fff2 2002000a c 20100000 22100001 102020
  //   20020022 c 22100002 102020 20020022 c 22100003 102020 20020022 c 22100004 102020 20020022 c 22100005
  //   102020 20020022 c 22100006 102020 20020022 c 22100007 102020 20020022 c 22100008 102020 20020022
  //   20020022 c 3e00008
endmodule

module PC_1 (
  input  [31:0] PC,
  output [31:0] PC_4
);

  // Incrementer incrementer_1: pin names not known; wires that end beside it: PC[31:2], PC_4[31:2]

  assign PC_4[1:0] = PC[1:0];
endmodule

module MIPS_Controller (
  input  [5:0] OP,
  input  [5:0] Funct,
  output [27:0] \控制信号 
);

  ROM #(.addrWidth(12), .dataWidth(28)) rom_1 (.addr({OP, Funct}), .data(\控制信号 ));  // open: sel

  // Notes on the sheet:
  //   contents of rom_1 (hex, n*v repeats v):
  //   28b000 0 228b000 128b000 0 0 228c000 0 300 0 0 0 6c02010 19*0 5280000 5280000 6280000 0 7280000
  //   8280000 0 a280000 0 0 b280000 c280000 20*0 64*b000820 64*200 64*1c0200 64*880 64*840 128*0
  //   128*5082800 64*b082800 64*c082800 64*7082c00 64*8082c00 1216*0 64*50b2800 64*0 64*50a2800 448*0
  //   64*5002808
endmodule
